# Fritzing sketch pushbutton-led-joystick (saved by Fritzing 0.9.4)
breadboards: 1

parts:
  Mod1 = ESP32-TTGO-T-DISPLAY
  R1 = Resistor [tolerance=±5% resistance=220 package="2512 [SMD]"]
  LED1 = LED - 5mm [color="Red (633nm)" package="5 mm [THT]"]
  S1 = Pushbutton [package="[SMD]"]
  Part2 = Black Joystick KY-023

nets:
  N1: Mod1.G-1, Mod1.G-2, Mod1.G-10, Mod1.G-11, Mod1.G-14, LED1.anode, S1.Pin_1, S1.Pin_2, Part2.GND
  N2: Mod1.2, S1.Pin_3, S1.Pin_4
  N3: Mod1.15, R1.Pin_0
  N4: Mod1.3V, Part2.+5V
  N5: Mod1.33, Part2.SW
  N6: Mod1.32, Part2.VRy
  N7: Mod1.39, Part2.VRx
  N8: R1.Pin_1, LED1.cathode

custom parts:
  ESP32-TTGO-T-DISPLAY: LILYGO TTGO T-Display GD32VF103CBT6 Main Chip ST7789 1.14 Inch IPS 240x135 Resolution Minimalist Development Board.
  Black Joystick KY-023: Description: The joystick is a combination of 2 analoog potentiometer and a digital switch. Arduino GND --> Module pin - Arduino +5V --> Module pin +5V Arduino Analoog 0 --> Module VRx Arduino Analoog 1 --> Module VRy Arduino Digital --> Module SW Dimensions: 1" x 1.25"
