# Fritzing sketch pushbutton-led (saved by Fritzing 0.9.4)
breadboards: 1

parts:
  Mod1 = ESP32-TTGO-T-DISPLAY
  R1 = Resistor [tolerance=±5% resistance=220 package="2512 [SMD]"]
  LED1 = LED - 5mm [color="Red (633nm)" package="5 mm [THT]"]
  S1 = Pushbutton [package="[SMD]"]

nets:
  N1: Mod1.G-1, Mod1.G-2, Mod1.G-10, Mod1.G-11, Mod1.G-14, LED1.anode, S1.Pin_1, S1.Pin_2
  N2: Mod1.2, S1.Pin_3, S1.Pin_4
  N3: Mod1.32, R1.Pin_0
  N4: R1.Pin_1, LED1.cathode

custom parts:
  ESP32-TTGO-T-DISPLAY: LILYGO TTGO T-Display GD32VF103CBT6 Main Chip ST7789 1.14 Inch IPS 240x135 Resolution Minimalist Development Board.
